// Logisim project discrete-project.circ as structural Verilog: 2 circuits, main circuit main
module main (
);

  // AND_Gate and_1 is placed but not wired
  // OR_Gate or_1 is placed but not wired
  // OR_Gate or_2 is placed but not wired
endmodule

module Muller_C (
  input  in_1,
  input  in_2,
  output out_3
);

  wire and_1_out, and_2_out, or_1_out;

  or or_1 (or_1_out, out_3, in_1);
  and and_1 (and_1_out, or_1_out, in_2);
  and and_2 (and_2_out, in_1, out_3);
  or or_2 (out_3, and_1_out, and_2_out);
endmodule
