// Logisim project gROUP-30_DISCRETE.circ as structural Verilog: 1 circuit, main circuit main
module main (
  input  Xn,
  input  Yn,
  output Zn
);

  wire and_1_out, and_2_out, or_1_out;

  and and_1 (and_1_out, Zn, Xn);
  or or_1 (or_1_out, Xn, Zn);
  and and_2 (and_2_out, or_1_out, Yn);
  or or_2 (Zn, and_1_out, and_2_out);

  // Notes on the sheet:
  //   Zn = (Xn + Zn-1) + (Yn * (Xn + Zn-1) 
endmodule
